// Digital circuit CPU.dig as structural Verilog
module CPU (
  input  [63:0] Databus_Manual_Input,
  input  CPU_Clock,
  input  in_3,
  input  in_4,
  input  in_5,
  input  in_6,
  input  [3:0] in_7,
  input  in_8,
  input  in_9,
  input  in_10,
  input  in_11,
  input  in_12
);

  wire alu_1_equal_to, alu_1_greater_than, alu_1_lesser_than, clock, Databus_Manual_Switch_out, driver_5_out,
       ETf, GTf, LTf, Manual_Clock_Stepper_out, Manual_Stepping_out;
  wire [23:0] Address_Register_q;
  wire [63:0] alu_1_x, databus, RA, Register_B_q, Sum_Register_q;

  Register #(.Bits(64)) Register_A (.D(databus), .C(clock), .en(in_4), .Q(RA));
  Register #(.Bits(64)) Register_B (.D(databus), .C(clock), .en(in_6), .Q(Register_B_q));
  DipSwitch #(.dipDefault("true")) Manual_Stepping (.out(Manual_Stepping_out));
  Button Manual_Clock_Stepper (.out(Manual_Clock_Stepper_out));
  assign clock = Manual_Stepping_out ? Manual_Clock_Stepper_out : 1'bz;  // Driver driver_1
  assign clock = ~Manual_Stepping_out ? CPU_Clock : 1'bz;  // DriverInvSel driverinvsel_1
  assign databus = Databus_Manual_Switch_out ? Databus_Manual_Input : 64'bz;  // Driver driver_2
  DipSwitch Databus_Manual_Switch (.out(Databus_Manual_Switch_out));
  assign databus = in_3 ? RA : 64'bz;  // Driver driver_3
  assign databus = in_5 ? Register_B_q : 64'bz;  // Driver driver_4
  ALU alu_1 (
    .A(RA), .B(databus), .Operation(in_7), .X(alu_1_x), .Lesser_Than(alu_1_lesser_than),
    .Equal_To(alu_1_equal_to), .Greater_Than(alu_1_greater_than));
  Register #(.Bits(24)) Address_Register (.D(databus[23:0]), .C(clock), .en(in_11), .Q(Address_Register_q));
  Register #(.Bits(64)) Sum_Register (.D(alu_1_x), .C(clock), .en(in_8), .Q(Sum_Register_q));
  assign driver_5_out = in_8 ? clock : 1'bz;  // Driver driver_5
  D_FF LT_Reg (.D(alu_1_lesser_than), .C(driver_5_out), .Q(LTf));  // open: nQ
  D_FF ET_Reg (.D(alu_1_equal_to), .C(driver_5_out), .Q(ETf));  // open: nQ
  D_FF GT_Reg (.D(alu_1_greater_than), .C(driver_5_out), .Q(GTf));  // open: nQ
  assign databus = in_9 ? Sum_Register_q : 64'bz;  // Driver driver_6
  RAMDualPort #(.AddrBits(24), .Bits(64)) ramdualport_1 (
    .A(Address_Register_q), .Din(databus), .str(in_12), .C(clock), .ld(in_10), .D(databus));

  // Other names for the same wires on the sheet: ADDRw = in_11; ALUop[3:0] = in_7; RAMr = in_10; RAMw = in_12;
  //   RAr = in_3; RAw = in_4; RBr = in_5; RBw = in_6; SRr = in_9; SRw = in_8

  // Notes on the sheet:
  //   Clock Control
  //   Manual Databus Control
  //   Register A
  //   Register B
  //   ALU & Sum Register
  //   Manual Inputs
  //   RAM & Address Register
endmodule
